# Fritzing sketch esquema (saved by Fritzing 0.9.4)

parts:
  Componente1 = Arduino Uno (Rev3)
  BT1 = Bluetooth HC-06u [package=THT]
  8x8_LED_Modul_mit_MAX1 = 8x8 LED Modul mit MAX7219 [package=THT]

nets:
  N1: Componente1.D10_PWM/SS, 8x8_LED_Modul_mit_MAX1.CS_Eingang
  N2: Componente1.D11_PWM/MOSI, 8x8_LED_Modul_mit_MAX1.CLK_Eingang
  N3: Componente1.D12/MISO, 8x8_LED_Modul_mit_MAX1.DIN_Eingang
  N4: Componente1.D2, BT1.RXD
  N5: Componente1.D3_PWM, BT1.TXD
  3V3: Componente1.3V3, BT1.VCC
  N6: Componente1.5V, 8x8_LED_Modul_mit_MAX1.VCC_Eingang
  GND: Componente1.GND, BT1.GND, 8x8_LED_Modul_mit_MAX1.GND_Eingang

custom parts:
  Bluetooth HC-06u: Bluetooth HC-06 - face up, pins down 16.5mm x 37.5mm PCB
